# Fritzing sketch StepperControl (saved by Fritzing 0.8.7b)
breadboards: 2

parts:
  U1 = atmega328 [part_number=ATmega328 package=dip]
  C3 = Ceramic Capacitor [capacitance=22pF package="0603 [SMD, multilayer]"]
  C4 = Ceramic Capacitor [capacitance=22pF package="0603 [SMD, multilayer]"]
  C5 = Ceramic Capacitor [capacitance="100 nF" package="0603 [SMD, multilayer]"]
  C6 = Ceramic Capacitor [capacitance="100 nF" package="0603 [SMD, multilayer]"]
  R1 = Resistor [tolerance=±5% resistance=10k package=THT]
  XTAL1 = Crystal [frequency="16 Mhz" package=THT]
  Q3 = NPN-Transistor [part_number=BC547 package="TO92 [THT]"]
  Q4 = NPN-Transistor [part_number=BC547 package="TO92 [THT]"]
  Q2 = NPN-Transistor [part_number=BC547 package="TO92 [THT]"]
  Q1 = NPN-Transistor [part_number=BC547 package="TO92 [THT]"]
  R2 = Resistor [tolerance=±5% resistance=10k package=THT]
  R3 = Resistor [tolerance=±5% resistance=10k package=THT]
  R4 = Resistor [tolerance=±5% resistance=10k package=THT]
  R5 = Resistor [tolerance=±5% resistance=10k package=THT]
  D1 = Rectifier Diode [part_number=1N4001 package="300 mil [THT]"]
  D2 = Rectifier Diode [part_number=1N4001 package="300 mil [THT]"]
  D4 = Rectifier Diode [part_number=1N4001 package="300 mil [THT]"]
  D5 = Rectifier Diode [part_number=1N4001 package="300 mil [THT]"]
  D6 = Rectifier Diode [part_number=1N4001 package="300 mil [THT]"]
  D7 = Rectifier Diode [part_number=1N4001 package="300 mil [THT]"]
  D8 = Rectifier Diode [part_number=1N4001 package="300 mil [THT]"]
  M1 = Stepper Motor - Bipolar [part_number="Stepper from DVD drive"]
  D3 = Rectifier Diode [part_number=1N4001 package="300 mil [THT]"]

nets:
  N1: U1.RESET, R1.Pin_0
  5V: U1.VCC, U1.AVCC, C5.1, C6.0, R1.Pin_1
  GND: U1.GND, C3.0, C4.1, C5.0, C6.1, Q3.E, Q4.E, Q2.E, Q1.E
  N2: U1.XLAT1, C4.0, XTAL1.pin_1
  N3: U1.XLAT2, C3.1, XTAL1.pin_0
  N4: U1.A0, R2.Pin_0, D1.anode
  N5: U1.A1, R3.Pin_1, D3.anode
  N6: U1.A2, R4.Pin_0, D5.anode
  N7: U1.A3, R5.Pin_1, D7.anode
  N8: Q3.B, R3.Pin_0
  N9: Q3.C, D4.cathode
  N10: Q4.B, R5.Pin_0
  N11: Q4.C, D8.cathode
  N12: Q2.B, R4.Pin_1
  N13: Q2.C, D6.cathode
  N14: Q1.B, R2.Pin_1
  N15: Q1.C, D2.cathode
  N16: D1.cathode, D4.anode, M1.A
  N17: D2.anode, M1.C, D3.cathode
  N18: D5.cathode, D8.anode, M1.B
  N19: D6.anode, D7.cathode, M1.D

notes:
  Trivial stepper motor control
  Created by Gregor Ottmann, but released to the public domain.
  https://github.com/Zappes/avr-StepperControl
